# Fritzing sketch code5 (saved by Fritzing 0.9.4)

parts:
  hc-sr1 = hc-sr04
  パーツ1 = Arduino Uno (Rev3)

nets:
  VCC: hc-sr1.VCC, パーツ1.5V
  N1: hc-sr1.Trig, パーツ1.D13/SCK
  N2: hc-sr1.Echo, パーツ1.D2
  GND: hc-sr1.GND, パーツ1.GND
