# Fritzing sketch code6 (saved by Fritzing 0.9.4)
breadboards: 1

parts:
  パーツ1 = Arduino Uno (Rev3)
  U1 = 7-SEGMENT-DISPLAY [package=7-segment-display]
  R1 = Resistor [tolerance=±5% resistance=220 package=THT]
  R2 = Resistor [tolerance=±5% resistance=220 package=THT]
  R3 = Resistor [tolerance=±5% resistance=220 package=THT]
  R4 = Resistor [tolerance=±5% resistance=220 package=THT]
  R5 = Resistor [tolerance=±5% resistance=220 package=THT]
  R6 = Resistor [tolerance=±5% resistance=220 package=THT]
  R7 = Resistor [tolerance=±5% resistance=220 package=THT]

nets:
  N1: パーツ1.D0/RX, R7.Pin_1
  N2: パーツ1.D1/TX, R6.Pin_1
  N3: パーツ1.D2, R5.Pin_1
  N4: パーツ1.D3_PWM, R4.Pin_1
  N5: パーツ1.D4, R3.Pin_1
  N6: パーツ1.D5_PWM, R2.Pin_1
  N7: パーツ1.D6_PWM, R1.Pin_1
  N8: パーツ1.GND, U1.F
  N9: U1.E, R1.Pin_0
  N10: U1.D, R3.Pin_0
  N11: U1.G1, R4.Pin_0
  N12: U1.DP, R5.Pin_0
  N13: U1.A, R6.Pin_0
  N14: U1.G2, R7.Pin_0
  N15: U1.G, R2.Pin_0

notes:
  220Ω
  a
  g
  f
  e
  d
  c
  b
