# Fritzing sketch code7 (saved by Fritzing 0.9.4)
breadboards: 1

parts:
  J1 = Basic Servo
  S1 = Pushbutton [package="[THT]"]
  S2 = Pushbutton [package="[THT]"]
  R1 = Resistor [tolerance=±5% resistance=220 package=THT]
  R2 = Resistor [tolerance=±5% resistance=220 package=THT]
  パーツ1 = Arduino Uno (Rev3)

nets:
  GND: J1.gnd, S1.Pin_3, S1.Pin_4, S2.Pin_3, S2.Pin_4, パーツ1.GND
  VCC: J1.vcc, R1.Pin_0, R2.Pin_0, パーツ1.5V
  N1: J1.pulse, パーツ1.D10_PWM/SS
  N2: S1.Pin_1, S1.Pin_2, R1.Pin_1, パーツ1.D1/TX
  N3: S2.Pin_1, S2.Pin_2, R2.Pin_1, パーツ1.D0/RX

notes:
  220Ω
