# Fritzing sketch code8 (saved by Fritzing 0.9.4)
breadboards: 1

parts:
  パーツ1 = Arduino Uno (Rev3)
  U1 = 7-SEGMENT-DISPLAY [package=7-segment-display]
  LED1 = LED - 5mm [color="Red (633nm)" package="5 mm [THT]"]
  LED2 = LED - 5mm [color="Red (633nm)" package="5 mm [THT]"]
  LED3 = LED - 5mm [color="Red (633nm)" package="5 mm [THT]"]
  R3 = Resistor [tolerance=±5% resistance=220 package=THT]
  R4 = Resistor [tolerance=±5% resistance=220 package=THT]
  R5 = Resistor [tolerance=±5% resistance=220 package=THT]
  R7 = Resistor [tolerance=±5% resistance=220 package=THT]
  R8 = Resistor [tolerance=±5% resistance=220 package=THT]
  R9 = Resistor [tolerance=±5% resistance=220 package=THT]
  R10 = Resistor [tolerance=±5% resistance=220 package=THT]
  R11 = Resistor [tolerance=±5% resistance=220 package=THT]
  R12 = Resistor [tolerance=±5% resistance=220 package=THT]
  R13 = Resistor [tolerance=±5% resistance=220 package=THT]
  J1 = Basic Servo

nets:
  N1: パーツ1.D10_PWM/SS, J1.pulse
  N2: パーツ1.D11_PWM/MOSI, R3.Pin_0
  N3: パーツ1.D12/MISO, R5.Pin_0
  N4: パーツ1.D13/SCK, R4.Pin_0
  N5: パーツ1.D0/RX, R13.Pin_1
  N6: パーツ1.D1/TX, R12.Pin_1
  N7: パーツ1.D2, R11.Pin_1
  N8: パーツ1.D3_PWM, R10.Pin_1
  N9: パーツ1.D4, R9.Pin_1
  N10: パーツ1.D5_PWM, R8.Pin_1
  N11: パーツ1.D6_PWM, R7.Pin_1
  5V: パーツ1.5V, J1.vcc
  GND: パーツ1.GND, U1.C, LED1.cathode, LED2.cathode, LED3.cathode, J1.gnd
  N12: U1.E, R7.Pin_0
  N13: U1.D, R9.Pin_0
  N14: U1.G1, R10.Pin_0
  N15: U1.DP, R11.Pin_0
  N16: U1.A, R12.Pin_0
  N17: U1.G2, R13.Pin_0
  N18: U1.G, R8.Pin_0
  N19: LED1.anode, R3.Pin_1
  N20: LED2.anode, R5.Pin_1
  N21: LED3.anode, R4.Pin_1

notes:
  220Ω
