# Fritzing sketch work1 (saved by Fritzing 0.9.4)
breadboards: 1

parts:
  R2 = Resistor [tolerance=±5% resistance=220 package=THT]
  LED2 = LED - 5mm [color="Red (633nm)" package="5 mm [THT]"]
  R3 = Resistor [tolerance=±5% resistance=220 package=THT]
  LED3 = LED - 5mm [color="Red (633nm)" package="5 mm [THT]"]
  パーツ1 = Arduino Uno (Rev3)

nets:
  N1: R2.Pin_0, パーツ1.D11_PWM/MOSI
  N2: R2.Pin_1, LED2.anode
  N3: LED2.cathode, LED3.cathode, パーツ1.GND
  N4: R3.Pin_0, パーツ1.D10_PWM/SS
  N5: R3.Pin_1, LED3.anode

notes:
  220Ω
