# Fritzing sketch work2 (saved by Fritzing 0.9.4)
breadboards: 1

parts:
  R1 = Resistor [tolerance=±5% resistance=220 package=THT]
  LED1 = LED - 5mm [color="Red (633nm)" package="5 mm [THT]"]
  パーツ1 = Arduino Uno (Rev3)

nets:
  N1: R1.Pin_0, パーツ1.D10_PWM/SS
  N2: R1.Pin_1, LED1.anode
  N3: LED1.cathode, パーツ1.GND

notes:
  220Ω
