# Fritzing sketch code1_2 (saved by Fritzing 0.9.4)
breadboards: 1

parts:
  Raspberry_Pi_2 = Raspberry Pi 3 [part_number=RPI-3-V1.2]
  R2 = Resistor [tolerance=±5% resistance=220 package=THT]
  LED2 = LED - 5mm [color="Red (633nm)" package="5 mm [THT]"]
  R3 = Resistor [tolerance=±5% resistance=220 package=THT]
  LED3 = LED - 5mm [color="Red (633nm)" package="5 mm [THT]"]
  R4 = Resistor [tolerance=±5% resistance=220 package=THT]
  LED4 = LED - 5mm [color="Red (633nm)" package="5 mm [THT]"]

nets:
  N1: Raspberry_Pi_2.GPIO10, R2.Pin_0
  N2: Raspberry_Pi_2.GPIO11, R3.Pin_0
  N3: Raspberry_Pi_2.GPIO12, R4.Pin_0
  N4: Raspberry_Pi_2.GND, LED2.cathode, LED3.cathode, LED4.cathode
  N5: R2.Pin_1, LED2.anode
  N6: R3.Pin_1, LED3.anode
  N7: R4.Pin_1, LED4.anode

notes:
  220Ω
