# Fritzing sketch code3 (saved by Fritzing 0.9.4)
breadboards: 1

parts:
  Raspberry_Pi_1 = Raspberry Pi 3 [part_number=RPI-3-V1.2]
  M1 = DC Motor
  U2 = TA7291P [package=HSIP10-P-2.54(THT)]

nets:
  N1: Raspberry_Pi_1.GPIO20, U2.IN2
  N2: Raspberry_Pi_1.GPIO16, U2.IN1
  GND: Raspberry_Pi_1.GND, U2.GND
  5V: Raspberry_Pi_1.5V, U2.Vcc
  N3: M1.pin_1, U2.OUT2
  N4: M1.pin_2, U2.OUT1

custom parts:
  TA7291P: The IC are Full-Bridge Driver. 4 modes available (CW / CCW / STOP / BRAKE) and PWM control. Output current:1.0 A (AVE.) 2.0 A (PEAK)
