# Fritzing sketch code6 (saved by Fritzing 0.9.4)
breadboards: 1

parts:
  7_Segment1 = 7 Segment Display
  Raspberry_Pi_1 = Raspberry Pi 3 [part_number=RPI-3-V1.2]

nets:
  N1: 7_Segment1.Segment_G, Raspberry_Pi_1.GPIO12
  N2: 7_Segment1.Segment_F, Raspberry_Pi_1.GPIO25
  N3: 7_Segment1.Segment_E, Raspberry_Pi_1.GPIO24
  N4: 7_Segment1.Segment_D, Raspberry_Pi_1.GPIO23
  N5: 7_Segment1.Segment_DP, Raspberry_Pi_1.GPIO16
  N6: 7_Segment1.Segment_C, Raspberry_Pi_1.GPIO18
  N7: 7_Segment1.Segment_B, Raspberry_Pi_1.GPIO15
  N8: 7_Segment1.Segment_A, Raspberry_Pi_1.GPIO14
