# Fritzing sketch code7 (saved by Fritzing 0.9.4)
breadboards: 1

parts:
  Raspberry_Pi_1 = Raspberry Pi 3 [part_number=RPI-3-V1.2]
  J1 = Basic Servo
  S1 = Pushbutton [package="[THT]"]
  S2 = Pushbutton [package="[THT]"]
  R1 = Resistor [tolerance=±5% resistance=220 package=THT]
  R2 = Resistor [tolerance=±5% resistance=220 package=THT]

nets:
  N1: Raspberry_Pi_1.GPIO11, S1.Pin_1, S1.Pin_2, R1.Pin_1
  N2: Raspberry_Pi_1.GPIO7, S2.Pin_1, S2.Pin_2, R2.Pin_1
  N3: Raspberry_Pi_1.GPIO23, J1.pulse
  GND: Raspberry_Pi_1.GND, J1.gnd, R1.Pin_0, R2.Pin_0
  5V: Raspberry_Pi_1.5V, J1.vcc, S1.Pin_3, S1.Pin_4, S2.Pin_3, S2.Pin_4
