# Fritzing sketch code8 (saved by Fritzing 0.9.4)
breadboards: 1

parts:
  Raspberry_Pi_2 = Raspberry Pi 3 [part_number=RPI-3-V1.2]
  7_Segment2 = 7 Segment Display
  R1 = Resistor [tolerance=±5% resistance=220 package=THT]
  R2 = Resistor [tolerance=±5% resistance=220 package=THT]
  R3 = Resistor [tolerance=±5% resistance=220 package=THT]
  LED1 = LED - 5mm [color="Red (633nm)" package="5 mm [THT]"]
  LED2 = smd LED [color="Orange (612nm)" package="1206 [SMD]"]
  LED3 = LED - 5mm [color="Yellow (595nm)" package="5 mm [THT]"]
  J1 = Basic Servo

nets:
  N1: Raspberry_Pi_2.GPIO17, R1.Pin_1
  N2: Raspberry_Pi_2.GPIO27, R2.Pin_1
  N3: Raspberry_Pi_2.GPIO22, R3.Pin_1
  N4: Raspberry_Pi_2.GPIO16, 7_Segment2.Segment_DP
  GND: Raspberry_Pi_2.GND, R1.Pin_0, R2.Pin_0, R3.Pin_0, LED1.cathode, LED1.anode, LED2.cathode, LED2.anode, LED3.cathode, LED3.anode, J1.gnd
  N5: Raspberry_Pi_2.GPIO12, 7_Segment2.Segment_G
  N6: Raspberry_Pi_2.GPIO25, 7_Segment2.Segment_F
  N7: Raspberry_Pi_2.GPIO24, 7_Segment2.Segment_E
  N8: Raspberry_Pi_2.GPIO23, 7_Segment2.Segment_D
  N9: Raspberry_Pi_2.GPIO18, 7_Segment2.Segment_C
  N10: Raspberry_Pi_2.GPIO15, 7_Segment2.Segment_B
  N11: Raspberry_Pi_2.GPIO14, 7_Segment2.Segment_A
  5V: Raspberry_Pi_2.5V, J1.vcc
